# Fritzing sketch fritzing_diagram (saved by Fritzing 1.0.3b)
breadboards: 1

parts:
  HC-SR04_Sensor_1 = HC-SR04 Ultrasonic Distance Sensor
  MCU1 = Raspberry Pi Zero
  R1 = Resistor [tolerance=±5% resistance=1k package="0603 [SMD]"]
  R2 = Resistor [tolerance=±5% resistance=2.2k package="0603 [SMD]"]
  LED1 = LED - 5mm [color="Red (633nm)" current=0.030A package="5 mm [THT]"]
  R3 = Resistor [tolerance=±5% resistance=220 package="0603 [SMD]"]
  M1 = IR break beam 3mm tx [package=THT]
  M2 = IR break beam 3mm rx [package=THT]
  LED3 = LED - 3mm [color="Green (560nm)" current=0.030A package="3 mm [THT]"]
  R4 = Resistor [tolerance=±5% resistance=220 package="0603 [SMD]"]

nets:
  N1: HC-SR04_Sensor_1.VCC, MCU1.pin_2, MCU1.pin_4, M1.pin1, M2.pin1
  N2: HC-SR04_Sensor_1.TRIG, MCU1.pin_16
  N3: HC-SR04_Sensor_1.ECHO, R1.Pin_0
  N4: HC-SR04_Sensor_1.GND, MCU1.pin_6, MCU1.pin_9, R2.Pin_1, LED1.cathode, M1.pin2, M2.pin3, LED3.cathode
  N5: MCU1.pin_18, R1.Pin_1, R2.Pin_0
  N6: MCU1.pin_22, R3.Pin_1
  N7: MCU1.pin_36, M2.pin2
  N8: MCU1.pin_37, R4.Pin_1
  N9: LED1.anode, R3.Pin_0
  N10: LED3.anode, R4.Pin_0

notes:
  Ultrasonic Sensor
  VCC : +ve rail
  TRIG: GPIO 23
  ECHO: 1kOhm - 2kOhm - GPIO 24
  GND: -ve rail
  Red LED
  ground: -ve rail
  vcc: 220ohm - GPIO 25
  Green LED
  ground: -ve rail
  vcc: 220ohm - GPIO 26
  IR Beam Sensor
  VCC : +ve rail
  Receiver: - GPIO 16
  GND: -ve rail
  Raspberry pi
  Pin 2 : +ve rail
  Pin 6: -ve rail
  Pin 16: TRIG
  Pin 18: ECHO
  Pin 22: Red LED
  Pin 36: Receiver
  Pin 37: Green LED

custom parts:
  IR break beam 3mm tx: Infrared break beam Sensor tx module.
  IR break beam 3mm rx: Infrared break beam Sensor rx module.
